# Fritzing sketch circuit (saved by Fritzing 0.9.0b)
breadboards: 1

parts:
  Part1 = Arduino Micro (Rev3)
  S1 = Pushbutton [package="[SMD]"]
  SP1 = SPEAKER [package=pcb_mount_speaker]
  R1 = Rotary Potentiometer (Small) [maximum_resistance=100kΩ package=THT]  # not connected

nets:
  N1: Part1.D8_PWM/A8, SP1.-
  N2: Part1.D12_PWM/A11, S1.Pin_3, S1.Pin_4
  N3: Part1.5V, S1.Pin_1, S1.Pin_2, SP1.+
